# Fritzing sketch Practica1 (saved by Fritzing 0.9.0b)
breadboards: 1

parts:
  LED1 = LED - 5mm [color="Red (633nm)" package="5 mm [THT]"]
  Parte1 = Arduino Uno (Rev3)

nets:
  N1: LED1.cathode, Parte1.GND
  N2: LED1.anode, Parte1.D13/SCK
