# Fritzing sketch Practica10 (saved by Fritzing 0.9.0b)
breadboards: 1

parts:
  J1 = Basic Servo
  J2 = Basic Servo
  Parte1 = Arduino Uno (Rev3)
  R1 = Rotary Potentiometer (Small) [maximum_resistance=100kΩ package=THT]
  R2 = Rotary Potentiometer (Small) [maximum_resistance=100kΩ package=THT]

nets:
  GND: J1.gnd, J2.gnd, Parte1.GND, R1.leg1, R2.leg1
  VCC: J1.vcc, J2.vcc, Parte1.5V, R1.leg2, R2.leg2
  N1: J1.pulse, Parte1.D10_PWM/SS
  N2: J2.pulse, Parte1.D3_PWM
  N3: Parte1.A0, R1.wiper
  N4: Parte1.A1, R2.wiper
