# Fritzing sketch Practica#1Teclado4x4 (saved by Fritzing 0.9.2b)

parts:
  Parte1 = Arduino Uno (Rev3)
  Matrix_keypad1 = KEYPAD 4x4

nets:
  N1: Parte1.D8, Matrix_keypad1.col2
  N2: Parte1.D9_PWM, Matrix_keypad1.col1
  N3: Parte1.D2, Matrix_keypad1.row4
  N4: Parte1.D3_PWM, Matrix_keypad1.row3
  N5: Parte1.D4, Matrix_keypad1.row2
  N6: Parte1.D5_PWM, Matrix_keypad1.row1
  N7: Parte1.D6_PWM, Matrix_keypad1.col4
  N8: Parte1.D7, Matrix_keypad1.col3

custom parts:
  KEYPAD 4x4: Matrix keypad 16 buttons, 4 rows x 4 columns

// code stored in the sketch: Teclado4x4.ino
/*  ----------------------------------------------------------------
    www.prometec.net
    Prog_19_1
    
    Leyendo un keypad de 4x4
--------------------------------------------------------------------  
*/

#include <Keypad.h>

const byte Filas = 4; 		//Cuatro filas
const byte Cols = 4; 		//Cuatro columnas

byte Pins_Filas[] = {9, 8, 7, 6};	 //Pines Arduino a los que contamos las filas.
byte Pins_Cols[] = { 5, 4, 3, 2}; 	// Pines Arduino a los que contamos las columnas.
char Teclas [ Filas ][ Cols ] = 
{
  {'1','2','3','A'},
  {'4','5','6','B'},
  {'7','8','9','C'},
  {'*','0','#','D'}
};

Keypad Teclado1 = Keypad(makeKeymap(Teclas), Pins_Filas, Pins_Cols, Filas, Cols);

void setup()
{	  Serial.begin(9600) ; }
  
void loop()
{	  char pulsacion = Teclado1.getKey() ; 
	  if (pulsacion != 0)			// Si el valor es 0 es que no se ha pulsado ninguna tecla
    		Serial.println(pulsacion);	

}
