# Fritzing sketch Practica#2Relevador (saved by Fritzing 0.9.2b)
breadboards: 1

parts:
  Parte1 = Arduino Uno (Rev3)
  R1 = Resistor [tolerance=±5% resistance=1k package=THT]
  D1 = Rectifier Diode [part_number=1N4001 package="300 mil [THT]"]
  VCC1 = Battery
  LED1 = LED - 5mm [color="Red (633nm)" package="5 mm [THT]"]
  U1 = RELAY [package=relay-g5q]
  Q1 = NPN-Transistor [package="TO92 [THT]"]

nets:
  N1: Parte1.D8, R1.Pin_1
  N2: Parte1.5V, Q1.E
  N3: Parte1.GND, D1.cathode, U1.COIL2
  N4: R1.Pin_0, Q1.B
  N5: D1.anode, U1.COIL1, Q1.C
  N6: VCC1.-, LED1.cathode
  N7: VCC1.+, U1.MAIN
  N8: LED1.anode, U1.NO

// code stored in the sketch: rele.ino
/*
Enciende y apaga una bombilla de 220V, cada 2 segundos, mediante
un rel? conectado al PIN 8 de Arduino
*/

int relayPin = 8;
// PIN al que va conectado el rel?

void setup(){
	pinMode(relayPin, OUTPUT);
}

void loop() {
	digitalWrite(relayPin, HIGH);
	delay(2000);
  digitalWrite(relayPin, LOW);
  delay(2000);
// ENCENDIDO
// APAGADO
}

// code stored in the sketch: relevador.ino
/*
Enciende y apaga una bombilla de 220V, cada 2 segundos, mediante
un relé conectado al PIN 8 de Arduino
*/

int relayPin = 8;
// PIN al que va conectado el relé

void setup(){
	pinMode(relayPin, OUTPUT);
}

void loop() {
	digitalWrite(relayPin, HIGH);
	delay(2000);
  digitalWrite(relayPin, LOW);
  delay(2000);
// ENCENDIDO
// APAGADO
}
