# Fritzing sketch Practica#3Sensor-temperatura (saved by Fritzing 0.9.2b)
breadboards: 1

parts:
  T1 = LM35 Temperature Sensor [package="TO92 [THT]"]
  Parte1 = Arduino Uno (Rev3)

nets:
  N1: T1.+Vs, Parte1.5V
  N2: T1.Vout, Parte1.A0
  GND: T1.GND, Parte1.GND

// code stored in the sketch: temperatura.ino
int analog_pin = 0;
float temperatura;
void setup () {
  Serial.begin(9600);
}
void loop() {
  temperatura = analogRead(analog_pin);
  temperatura = 5.0*temperatura*100.0/1024.0;
  Serial.print(temperatura);
  Serial.println(" oC");
  delay(1000);
}
