# Fritzing sketch Practica#5Pantalla-LCD-Keyboard (saved by Fritzing 0.9.2b)
breadboards: 1

parts:
  Parte1 = Arduino Uno (Rev3)
  R1 = Rotary Potentiometer (Small) [maximum_resistance=100kΩ package=THT]
  LCD1 = LCD screen
  R2 = Resistor [tolerance=±5% resistance=220 package=THT]
  Matrix_keypad1 = KEYPAD 4x4

nets:
  N1: Parte1.A1, Matrix_keypad1.col1
  N2: Parte1.A2, Matrix_keypad1.col2
  N3: Parte1.A3, Matrix_keypad1.col3
  N4: Parte1.A4/SDA, Matrix_keypad1.col4
  N5: Parte1.A5/SCL, Matrix_keypad1.row1
  N6: Parte1.D8, LCD1.DB4
  N7: Parte1.D11_PWM/MOSI, LCD1.E
  N8: Parte1.D12/MISO, LCD1.RS
  GND: Parte1.GND, R1.leg2, LCD1.VSS, LCD1.R/W, LCD1.LED-
  N9: Parte1.D2, Matrix_keypad1.row4
  N10: Parte1.D3_PWM, Matrix_keypad1.row3
  N11: Parte1.D4, Matrix_keypad1.row2
  N12: Parte1.D5_PWM, LCD1.DB7
  N13: Parte1.D6_PWM, LCD1.DB6
  N14: Parte1.D7, LCD1.DB5
  5V: Parte1.5V, R1.leg1, LCD1.VDD, R2.Pin_1
  N15: R1.wiper, LCD1.V0
  N16: LCD1.LED+, R2.Pin_0

custom parts:
  KEYPAD 4x4: Matrix keypad 16 buttons, 4 rows x 4 columns

// code stored in the sketch: keyboard-LCD.ino
#include <LiquidCrystal.h>
#include <Keypad.h>

LiquidCrystal lcd(12, 11, 8, 7, 6, 5);
const byte Filas = 4;
const byte Cols = 4; 

byte Pins_Filas[] = {A5, 2, 3, 4};
byte Pins_Cols[] = { A1, A2, A3, A4}; 
char Teclas [ Filas ][ Cols ] = 
{
  {'1','2','3','A'},
  {'4','5','6','B'},
  {'7','8','9','C'},
  {'*','0','#','D'}
};

Keypad Teclado1 = Keypad(makeKeymap(Teclas), Pins_Filas, Pins_Cols, Filas, Cols);

void setup(){
lcd.begin(16,2);
lcd.print("Hola Viejo");
}

void loop(){
char pulsacion = Teclado1.getKey() ; 
if (pulsacion != 0){			
    lcd.setCursor(0,1);
    lcd.print(pulsacion);
}
}

// code stored in the sketch: lcd-lm35.ino
#include <LiquidCrystal.h>

LiquidCrystal lcd(12, 11, 5, 4, 3, 2);

//Hasta aqu? hemos declarado la librer?a para la LCD y los pines por donde le va a entrar la informaci?n.

float centi()
{// Funcion para leer el dato analogico y convertirlo a digital:
  int dato;
  float c;
  dato=analogRead(A0);
  
  c = (500.0 * dato)/1023;
  //Esta f?rmula sale de la relaci?n del sensor con los grados. ?sta es f?cilmente rastreable por la web pero vamos a intentar explicarla un poco: El sensor de temperatura LM35 responde a variaciones de 10 mV por cada grado cent?grado. Si el sensor detecta 1 grado cent?grado a la salida del sensor obtendr?amos 10 mV. Ejemplo: 26,4?C = 264 mV = 0.264 V.
//Tenemos que el convertidor de anal?gico a digital es de 10 bits de resoluci?n, los valores variar?n entre 0 y 1023, entonces Vout= (5V*Dato)/1023 siendo  ( 0 < Dato < 1023 ) y para ajustar la escala a grados cent?grados: Vout = ((5V*Dato)*100)/1023
  return (c);
}


float kelvin(float cent)
{
  float k;
  k=cent+273.15;
  return(k);
}

float fahren(float cent)
{
  float f;
  f=cent*1.8+32;
  return (f);
}


float rankin(float cent)
{
  float r;
  r=(cent + 273.15)*1.8;
  return (r);
}

//Hasta aqu? hemos declarado las funciones de conversi?n del dato anal?gico de entrada del sensor en grados celsius en sus respectivas equivalencias.

void setup() {
  // Definimos la LCD con dimension 2x16 y definimos los caracteres que deben salir en las filas:
lcd.begin(16,2);
lcd.print("C=      K=");
lcd.setCursor(0,1);
lcd.print("Temperatura");
}

//Hasta aqu? hemos definido qu? queremos que salga impreso por la pantalla y el tama?o de ?sta.
void loop() {
  // put your main code here, to run repeatedly: 
  float Centigrados = centi();
  float Fahrenheit = fahren (Centigrados);
  float Rankin = rankin (Centigrados);
  float Kelvin = kelvin (Centigrados);
  lcd.setCursor(2,0);
  lcd.print(Centigrados);
  lcd.setCursor(10,0);
  lcd.print(Kelvin);
  delay(200);
  //Por ?ltimo, hemos usado la parte activa del programa o bucle para que constantemente para cada variaci?n recalcule los datos. 
  
}
