# Fritzing sketch Practica#3Conf-bluetooth (saved by Fritzing 0.9.2b)

parts:
  Parte1 = Arduino Uno (Rev3)
  Parte2 = Bluetooth Mate Silver

nets:
  N1: Parte1.D0/RX, Parte2.RX_5V
  N2: Parte1.D1/TX, Parte2.TX_5V
  5V: Parte1.5V, Parte2.VCC
  GND: Parte1.GND, Parte2.GND

// code stored in the sketch: conf-bluetooth.ino
#include <SoftwareSerial.h>

SoftwareSerial blue(0,1);
char NOMBRE[15]  = "Pussybreaker";    
char BPS         = '4';   // 1=1200 , 2=2400, 3=4800, 4=9600, 5=19200, 6=38400, 7=57600, 8=115200
char PASS[10]    = "1207";        
 
void setup()
{
    blue.begin(9600);
    pinMode(13,OUTPUT);
    digitalWrite(13,HIGH);
    delay(4000);
    digitalWrite(13,LOW);
    
    blue.print("AT"); 
    delay(1000);
 
    blue.print("AT+NAME"); 
    blue.print(NOMBRE);
    delay(1000);
 
    blue.print("AT+BAUD"); 
    blue.print(BPS); 
    delay(1000);
 
    blue.print("AT+PIN");
    blue.print(PASS); 
    delay(1000);    
}
 
void loop()
{
    digitalWrite(13, !digitalRead(13));
    delay(500);
}
