# Fritzing sketch Practica#4App-bluetooth (saved by Fritzing 0.9.2b)

parts:
  Parte1 = Arduino Uno (Rev3)
  Parte2 = Bluetooth Mate Silver
  R3 = Resistor [tolerance=±5% resistance=220 package=THT]
  LED1 = LED - 5mm [color="Red (633nm)" package="5 mm [THT]"]

nets:
  GND: Parte1.GND, Parte2.GND, LED1.cathode
  N1: Parte1.D0/RX, Parte2.RX_5V
  N2: Parte1.D1/TX, Parte2.TX_5V
  N3: Parte1.D5_PWM, R3.Pin_0
  5V: Parte1.5V, Parte2.VCC
  N4: R3.Pin_1, LED1.anode

// code stored in the sketch: conf-bluetooth.ino
#include <SoftwareSerial.h>

#define RxD 0
#define TxD 1
#define RST 3
#define KEY 4

SoftwareSerial BTSerial(RxD, TxD);

void setup()
{
  
  pinMode(RST, OUTPUT);
  pinMode(KEY, OUTPUT);
  digitalWrite(RST, LOW);
  digitalWrite(KEY, HIGH);
  digitalWrite(RST, HIGH);
  
  delay(500);
  
  BTSerial.flush();
  delay(500);
  BTSerial.begin(38400);
  Serial.begin(9600);
  Serial.println("Enter AT commands:");

  BTSerial.print("AT\r\n");
  delay(100);

}

void loop()
{

  if (BTSerial.available())
    Serial.write(BTSerial.read());

  if (Serial.available())
    BTSerial.write(Serial.read());

}

// code stored in the sketch: led-bluetooth.ino
char command;
String string;
boolean ledon = false;
#define led 5

void setup(){
    Serial.begin(9600);
    pinMode(led, OUTPUT);
}

void loop(){
    if (Serial.available() > 0) {
		string = "";
	}
    while(Serial.available() > 0){
      command = ((byte)Serial.read());
      
      if(command == ':'){
        break;
      }else{
        string += command;
      }
      delay(1);
    }
    
    if(string == "TO"){
        ledOn();
        ledon = true;
    }
    
    if(string =="TF"){
        ledOff();
        ledon = false;
        Serial.println(string);
    }
    
    if ((string.toInt()>=0)&&(string.toInt()<=255)){
      if (ledon==true){
        analogWrite(led, string.toInt());
        Serial.println(string);
        delay(10);
      }
    }
}

void ledOn(){
      analogWrite(led, 255);
      delay(10);
}
 void ledOff(){
      analogWrite(led, 0);
      delay(10);
}
