# Fritzing sketch Practica#7Control-PID (saved by Fritzing 0.9.2b)
circuit board: 26.8676cm x 8.33025cm
breadboards: 1

parts:
  Parte1 = Arduino Uno (Rev3)
  D1 = Rectifier Diode [part_number=1N4001 package="300 mil [THT]"]
  U1 = RELAY [package=relay-g5q]
  Q1 = NPN-Transistor [package="TO92 [THT]"]
  T1 = LM35 Temperature Sensor [package="TO92 [THT]"]
  R1 = Resistor [tolerance=±5% resistance=1k package=THT]
  Matrix_keypad1 = KEYPAD 4x4
  R2 = Resistor [tolerance=±5% resistance=220 package=THT]
  J1 = Screw terminal - 2 pins [package=THT]
  LCD1 = LCD screen
  R3 = Rotary Potentiometer (Small) [maximum_resistance=10kΩ package=THT]

nets (from the schematic view):
  N1: Parte1.A0, T1.Vout
  N2: Parte1.A1, Matrix_keypad1.col1
  N3: Parte1.A2, Matrix_keypad1.col2
  N4: Parte1.A3, Matrix_keypad1.col3
  N5: Parte1.A4/SDA, Matrix_keypad1.col4
  N6: Parte1.A5/SCL, Matrix_keypad1.row1
  N7: Parte1.D8, LCD1.DB6
  N8: Parte1.D9_PWM, LCD1.DB5
  N9: Parte1.D10_PWM/SS, LCD1.DB4
  N10: Parte1.D11_PWM/MOSI, LCD1.E
  N11: Parte1.D12/MISO, LCD1.RS
  N12: Parte1.D13/SCK, R1.Pin_1
  N13: Parte1.D2, Matrix_keypad1.row2
  N14: Parte1.D3_PWM, Matrix_keypad1.row3
  N15: Parte1.D4, Matrix_keypad1.row4
  N16: Parte1.D7, LCD1.DB7
  5V: Parte1.5V, D1.cathode, U1.COIL2, T1.+Vs, R2.Pin_1, LCD1.VDD, R3.leg1
  GND: Parte1.GND, Q1.E, T1.GND, LCD1.VSS, LCD1.R/W, LCD1.LED-, R3.leg2
  N17: D1.anode, U1.COIL1, Q1.C
  N18: U1.MAIN, J1.pin2
  N19: U1.NO, J1.pin1
  N20: Q1.B, R1.Pin_0
  N21: R2.Pin_0, LCD1.LED+
  N22: LCD1.V0, R3.wiper

custom parts:
  KEYPAD 4x4: Matrix keypad 16 buttons, 4 rows x 4 columns

// code stored in the sketch: on-off.ino
#include <LiquidCrystal.h>
#include <Keypad.h>
#include <EEPROM.h>

const int analog_pin = 0;
const int foco = 6;
const byte Filas = 4;
const byte Cols = 4;

LiquidCrystal lcd(12, 11, 10, 9, 8, 7);
byte Pins_Filas[] = {4, 3, 2, A5};
byte Pins_Cols[] = { A4, A3, A2, A1}; 
char Teclas [ Filas ][ Cols ] = 
{
  {'1','2','3','A'},
  {'4','5','6','B'},
  {'7','8','9','C'},
  {'%','0','#','D'}
};
Keypad Teclado1 = Keypad(makeKeymap(Teclas), Pins_Filas, Pins_Cols, Filas, Cols);

void setup(){
  pinMode(foco, OUTPUT);
  lcd.begin(16,2);
  lcd.print("Temp:          C");
  lcd.setCursor(0,1);
  lcd.print("Refer:         C");
}

void loop(){
  float referencia= EEPROM.read(0);
  char pulsacion = Teclado1.getKey() ; 
  switch(pulsacion){
    case '1': referencia += 1; break;
    case '2': referencia += 10; break;
    case '3': referencia += 20; break;
    case '4': referencia += 30; break;
    case '5': referencia += 40; break;
    case '6': referencia += 50; break;
    case '7': referencia -= 1; break;
    case '8': referencia -= 10; break;
    case '9': referencia -= 20; break;
    case '%': referencia -= 30; break;
    case '0': referencia -= 40; break;
    case '#': referencia -= 50; break;
    case 'A': referencia = 0; break;
    case 'B': referencia = 100; break;
    case 'C': referencia = -100; break;
  }
  EEPROM.write(0,referencia);
  
  float temperatura = analogRead(analog_pin);
  temperatura = 5.0*temperatura*100.0/1024.0;
  lcd.setCursor(9,0);
  lcd.print(temperatura);
  lcd.setCursor(9,1);
  lcd.print(referencia);
  
  if(temperatura<=referencia){
    digitalWrite(foco, HIGH);
  }else{ 
    digitalWrite(foco, LOW);
  }
  delay(800);
}

// code stored in the sketch: pid.ino
#include <LiquidCrystal.h>
#include <Keypad.h>
#include <EEPROM.h>
#include <PID_v1.h>

const int analog_pin = 0;
const int foco = 6;
const byte Filas = 4;
const byte Cols = 4;

LiquidCrystal lcd(12, 11, 10, 9, 8, 7);
byte Pins_Filas[] = {4, 3, 2, A5};
byte Pins_Cols[] = { A4, A3, A2, A1}; 
char Teclas [ Filas ][ Cols ] = {
  {'1','2','3','A'},
  {'4','5','6','B'},
  {'7','8','9','C'},
  {'%','0','#','D'}
};
Keypad Teclado1 = Keypad(makeKeymap(Teclas), Pins_Filas, Pins_Cols, Filas, Cols);

double temperatura, referencia, salida;
double Kp=200, Ki=50, Kd=100;
PID myPID(&temperatura, &salida, &referencia, Kp, Ki, Kd, DIRECT);

int WindowSize = 5000;
unsigned long windowStartTime;

void setup(){
	Serial.begin(9600);
  pinMode(foco, OUTPUT);
  lcd.begin(16,2);
  lcd.print("Temp:          C");
  lcd.setCursor(0,1);
  lcd.print("Refer:         C");
	windowStartTime = millis();
  referencia= EEPROM.read(0);
	temperatura= EEPROM.read(1);
  myPID.SetOutputLimits(0, WindowSize);
  myPID.SetMode(AUTOMATIC);
	
}

void loop(){
  referencia= EEPROM.read(0);
  char pulsacion = Teclado1.getKey() ; 
  switch(pulsacion){
    case '1': referencia += 1; break;
    case '2': referencia += 10; break;
    case '3': referencia += 20; break;
    case '4': referencia += 30; break;
    case '5': referencia += 40; break;
    case '6': referencia += 50; break;
    case '7': referencia -= 1; break;
    case '8': referencia -= 10; break;
    case '9': referencia -= 20; break;
    case '%': referencia -= 30; break;
    case '0': referencia -= 40; break;
    case '#': referencia -= 50; break;
    case 'A': referencia = 0; break;
    case 'B': referencia = 100; break;
    case 'C': referencia = -100; break;
  }
  EEPROM.write(0,referencia);
  
  for(int i=0;i<30;i++){temperatura = analogRead(analog_pin)};
  temperatura = 5.0*temperatura*100.0/1024.0;
	EEPROM.write(1,temperatura);
  lcd.setCursor(9,0);
  lcd.print(temperatura);
  lcd.setCursor(9,1);
  lcd.print(referencia);

	myPID.Compute();

  if(millis() - windowStartTime > WindowSize){
    windowStartTime += WindowSize;
  }
  if(salida < millis() - windowStartTime){ 
		digitalWrite(foco, HIGH);
	}
  else{ 
		digitalWrite(foco, LOW);
	}

	Serial.println(referencia);
	Serial.println(temperatura);
	Serial.println(salida);
  delay(1000);
}

// code stored in the sketch: proporcional.ino
#include <LiquidCrystal.h>
#include <Keypad.h>
#include <EEPROM.h>

const int analog_pin = 0;
const int foco = 6;
const byte Filas = 4;
const byte Cols = 4;

LiquidCrystal lcd(12, 11, 10, 9, 8, 7);
byte Pins_Filas[] = {4, 3, 2, A5};
byte Pins_Cols[] = { A4, A3, A2, A1}; 
char Teclas [ Filas ][ Cols ] = {
  {'1','2','3','A'},
  {'4','5','6','B'},
  {'7','8','9','C'},
  {'%','0','#','D'}
};
Keypad Teclado1 = Keypad(makeKeymap(Teclas), Pins_Filas, Pins_Cols, Filas, Cols);

float temperatura;float referencia;
int TiempoMuestreo=1;         // tiempo de muestreo Se encuentra en milisegundos
unsigned long pasado=0;       // tiempo pasado (Se hace para asegurar tiempo de muestreo)
unsigned long ahora;
float error;              // error
int U;                  // Señal control
// constantes del controlador 
int Kp=2000; 

void setup(){
  pinMode(foco, OUTPUT);
  lcd.begin(16,2);
  lcd.print("Temp:          C");
  lcd.setCursor(0,1);
  lcd.print("Refer:         C");
	referencia= EEPROM.read(0);
}

void loop(){
  referencia= EEPROM.read(0);
  char pulsacion = Teclado1.getKey() ; 
  switch(pulsacion){
    case '1': referencia += 1; break;
    case '2': referencia += 10; break;
    case '3': referencia += 20; break;
    case '4': referencia += 30; break;
    case '5': referencia += 40; break;
    case '6': referencia += 50; break;
    case '7': referencia -= 1; break;
    case '8': referencia -= 10; break;
    case '9': referencia -= 20; break;
    case '%': referencia -= 30; break;
    case '0': referencia -= 40; break;
    case '#': referencia -= 50; break;
    case 'A': referencia = 0; break;
    case 'B': referencia = 100; break;
    case 'C': referencia = -100; break;
  }
  EEPROM.write(0,referencia);
  
  temperatura = analogRead(analog_pin);
  temperatura = 5.0*temperatura*100.0/1024.0;
  lcd.setCursor(9,0);
  lcd.print(temperatura);
  lcd.setCursor(9,1);
  lcd.print(referencia);

	ahora=millis();         // tiempo actual 
   
  int CambioTiempo= ahora-pasado;      // diferencia de tiempo actual- pasado
  if(CambioTiempo >= TiempoMuestreo){  // si se supera el tiempo de muestreo
      error = referencia-temperatura;            // error (Lazo cerrado)-- Feedback
      U=(int)Kp*error;                 // Señal de control
      pasado=ahora;                // actualizar tiempo
  }

 	if (U<0){
   U = abs(U);
 	}
  
  if(temperatura<referencia){
    digitalWrite(foco, LOW);
		delay(U);
		digitalWrite(foco, HIGH);
		delay(100-U);
  }else{ 
    digitalWrite(foco, LOW);
  }
  delay(TiempoMuestreo);
}

// code stored in the sketch: rele.ino
/*
Enciende y apaga una bombilla de 220V, cada 2 segundos, mediante
un rel? conectado al PIN 8 de Arduino
*/

int relayPin = 8;
// PIN al que va conectado el rel?

void setup(){
	pinMode(relayPin, OUTPUT);
}

void loop() {
	digitalWrite(relayPin, HIGH);
	delay(2000);
  digitalWrite(relayPin, LOW);
  delay(2000);
// ENCENDIDO
// APAGADO
}

// code stored in the sketch: relevador.ino
/*
Enciende y apaga una bombilla de 220V, cada 2 segundos, mediante
un relé conectado al PIN 8 de Arduino
*/

int relayPin = 8;
// PIN al que va conectado el relé

void setup(){
	pinMode(relayPin, OUTPUT);
}

void loop() {
	digitalWrite(relayPin, HIGH);
	delay(2000);
  digitalWrite(relayPin, LOW);
  delay(2000);
// ENCENDIDO
// APAGADO
}
