# Fritzing sketch Practica2 (saved by Fritzing 0.9.0b)
breadboards: 1

parts:
  R1 = Resistor [tolerance=±5% resistance=220 package=THT]
  R2 = Resistor [tolerance=±5% resistance=220 package=THT]
  R3 = Resistor [tolerance=±5% resistance=220 package=THT]
  LED1 = LED - 5mm [color="Red (633nm)" package="5 mm [THT]"]
  LED2 = LED - 5mm [color="Yellow (595nm)" package="5 mm [THT]"]
  LED3 = LED - 5mm [color="Green (555nm)" package="5 mm [THT]"]
  Parte1 = Arduino Uno (Rev3)

nets (from the schematic view):
  N1: R1.Pin_0, LED1.anode
  N2: R1.Pin_1, Parte1.D11_PWM/MOSI
  N3: R2.Pin_0, LED2.anode
  N4: R2.Pin_1, Parte1.D10_PWM/SS
  N5: R3.Pin_0, LED3.anode
  N6: R3.Pin_1, Parte1.D9_PWM
  N7: LED1.cathode, LED2.cathode, LED3.cathode, Parte1.GND
