# Fritzing sketch Practica#2Motores (saved by Fritzing 0.9.2b)

parts:
  Parte1 = Arduino Uno (Rev3)
  M1 = DC Motor
  M2 = DC Motor
  S1 = H-Bridge with L298N
  VCC1 = Battery block 9V

nets:
  N1: Parte1.D2, S1.ENA
  N2: Parte1.D3_PWM, S1.IN1
  N3: Parte1.D4, S1.IN2
  N4: Parte1.D5_PWM, S1.IN3
  N5: Parte1.D6_PWM, S1.IN4
  N6: Parte1.D7, S1.ENB
  5V: Parte1.5V, S1.5V, VCC1.+
  GND: Parte1.GND, S1.GND, VCC1.-
  N7: M1.pin_1, M1.pin_2, M2.pin_1, S1.M1-02, S1.M2-01, S1.M2-02, S1.ENA-5V
  N8: M2.pin_2, S1.M1-01

custom parts:
  H-Bridge with L298N: h-bridge

// code stored in the sketch: MotorDC.ino
///
/// Ejemplo de control de Puente H
///
/// by RafaG
///
 
#include "PuenteH.h"
 
/// Definición de pines
///
 
// Motor A
const int ENA = 2; // Pin PWM
const int IN1 = 3;
const int IN2 = 4;
 
// Motor B
const int ENB = 7; // Pin PWM
const int IN3 = 6;
const int IN4 = 5;
///
/// Fin de definición de pines
 
/// Instancia a clase PuenteH
///
PuenteH puenteH(PuenteH::L298);
///
/// Fin de instancia a clase PuenteH
 
/// Funciones básicas
///
void setup() {
    Serial.begin(9600);
    Serial.println("Inicio de sistema:");
 
    puenteH.setMotor1(ENA, IN1, IN2);
    puenteH.setMotor2(ENB, IN3, IN4);
    puenteH.initMotors();
}
 
void loop() {
    puenteH.goForward(200);
    delay(1000);
    puenteH.goBackward(200);
    delay(1000);
    puenteH.turnLeft(200);
    delay(1000);
    puenteH.turnRight(200);
    delay(1000);
    puenteH.stop();
    delay(1000);
}
///
/// Fin funciones básicas

// code stored in the sketch: Teclado4x4.ino
/*  ----------------------------------------------------------------
    www.prometec.net
    Prog_19_1
    
    Leyendo un keypad de 4x4
--------------------------------------------------------------------  
*/

#include <Keypad.h>

const byte Filas = 4; 		//Cuatro filas
const byte Cols = 4; 		//Cuatro columnas

byte Pins_Filas[] = {9, 8, 7, 6};	 //Pines Arduino a los que contamos las filas.
byte Pins_Cols[] = { 5, 4, 3, 2}; 	// Pines Arduino a los que contamos las columnas.
char Teclas [ Filas ][ Cols ] = 
{
  {'1','2','3','A'},
  {'4','5','6','B'},
  {'7','8','9','C'},
  {'*','0','#','D'}
};

Keypad Teclado1 = Keypad(makeKeymap(Teclas), Pins_Filas, Pins_Cols, Filas, Cols);

void setup()
{	  Serial.begin(9600) ; }
  
void loop()
{	  char pulsacion = Teclado1.getKey() ; 
	  if (pulsacion != 0)			// Si el valor es 0 es que no se ha pulsado ninguna tecla
    		Serial.println(pulsacion);	

}
