# Fritzing sketch Practica#1Radar (saved by Fritzing 0.9.2b)

parts:
  Parte1 = Arduino Uno (Rev3)
  J1 = Basic Servo
  Parte2 = HC-SR04

nets:
  N1: Parte1.D8, J1.pulse
  N2: Parte1.D9_PWM, Parte2.Echo
  N3: Parte1.D10_PWM/SS, Parte2.Trig
  VCC: Parte1.5V, J1.vcc, Parte2.Vcc
  GND: Parte1.GND, J1.gnd, Parte2.Gnd

custom parts:
  HC-SR04: HC-SR04 ultrasonic distance sensor

// code stored in the sketch: Radar.ino
#include <Servo.h>
/ Includes the Servo library
#include <Servo.h>
// Defines Tirg and Echo pins of the Ultrasonic Sensor
const int trigPin = 10;
const int echoPin = 9;
// Variables for the duration and the distance
long duration;
int distance;
Servo myServo; // Creates a servo object for controlling the servo motor
void setup() {
  pinMode(trigPin, OUTPUT); // Sets the trigPin as an Output
  pinMode(echoPin, INPUT); // Sets the echoPin as an Input
  Serial.begin(9600);
  myServo.attach(8); // Defines on which pin is the servo motor attached
}
void loop() {
  // rotates the servo motor from 15 to 145 degrees
  for(int i=15;i<=145;i++){  
  myServo.write(i);
  delay(30);
  distance = calculateDistance();// Calls a function for calculating the distance measured by the Ultrasonic sensor for each degree
  
  Serial.print(i); // Sends the current degree into the Serial Port
  Serial.print(","); // Sends addition character right next to the previous value needed later in the Processing IDE for indexing
  Serial.print(distance); // Sends the distance value into the Serial Port
  Serial.print("."); // Sends addition character right next to the previous value needed later in the Processing IDE for indexing
  }
