# Fritzing sketch rfid-rc522 (saved by Fritzing 0.9.3b)
breadboards: 1

parts:
  Arduino_UNO = Arduino Uno (Rev3)
  RFID-RC522 = RFID-RC522-v2

nets:
  N1: Arduino_UNO.D9_PWM, RFID-RC522.RST
  N2: Arduino_UNO.D10_PWM/SS, RFID-RC522.SDA
  N3: Arduino_UNO.D11_PWM/MOSI, RFID-RC522.MOSI
  N4: Arduino_UNO.D12/MISO, RFID-RC522.MISO
  N5: Arduino_UNO.D13/SCK, RFID-RC522.SCK
  3V3: Arduino_UNO.3V3, RFID-RC522.3.3V
  GND: Arduino_UNO.GND, RFID-RC522.GND

custom parts:
  RFID-RC522-v2: A simple China made RFID-RC522 Reader; do check the pin labels, as this is a MFRC522 based clone.

// code stored in the sketch: controlAcceso.ino
#include <SPI.h>
#include <MFRC522.h>

#define RST_PIN	9    //Pin 9 para el reset del RC522
#define SS_PIN	10   //Pin 10 para el SS (SDA) del RC522
MFRC522 mfrc522(SS_PIN, RST_PIN); ///Creamos el objeto para el RC522

void setup() {
	Serial.begin(9600); //Iniciamos La comunicacion serial
	SPI.begin();        //Iniciamos el Bus SPI
	mfrc522.PCD_Init(); // Iniciamos el MFRC522
	Serial.println("Control de acceso:");
}

byte ActualUID[4]; //almacenará el código del Tag leído
byte Usuario1[4]= {0x4D, 0x5C, 0x6A, 0x45} ; //código del usuario 1
byte Usuario2[4]= {0xC1, 0x2F, 0xD6, 0x0E} ; //código del usuario 2
void loop() {
	// Revisamos si hay nuevas tarjetas  presentes
	if ( mfrc522.PICC_IsNewCardPresent()) 
        {  
  		//Seleccionamos una tarjeta
            if ( mfrc522.PICC_ReadCardSerial()) 
            {
                  // Enviamos serialemente su UID
                  Serial.print(F("Card UID:"));
                  for (byte i = 0; i < mfrc522.uid.size; i++) {
                          Serial.print(mfrc522.uid.uidByte[i] < 0x10 ? " 0" : " ");
                          Serial.print(mfrc522.uid.uidByte[i], HEX);   
                          ActualUID[i]=mfrc522.uid.uidByte[i];          
                  } 
                  Serial.print("     ");                 
                  //comparamos los UID para determinar si es uno de nuestros usuarios  
                  if(compareArray(ActualUID,Usuario1))
                    Serial.println("Acceso concedido...");
                  else if(compareArray(ActualUID,Usuario2))
                    Serial.println("Acceso concedido...");
                  else
                    Serial.println("Acceso denegado...");
                  
                  // Terminamos la lectura de la tarjeta tarjeta  actual
                  mfrc522.PICC_HaltA();
          
            }
      
	}
	
}

//Función para comparar dos vectores
 boolean compareArray(byte array1[],byte array2[])
{
  if(array1[0] != array2[0])return(false);
  if(array1[1] != array2[1])return(false);
  if(array1[2] != array2[2])return(false);
  if(array1[3] != array2[3])return(false);
  return(true);
}

// code stored in the sketch: read_writeRFID.ino
#include <SPI.h>
#include <MFRC522.h>

#define SS_PIN 10
#define RST_PIN 9
 
MFRC522 rfid(SS_PIN, RST_PIN);

MFRC522::MIFARE_Key key; 
// Init array that will store new NUID 
byte nuidPICC[3];

void setup() 
{ 
  Serial.begin(9600);
  SPI.begin();          // Init SPI bus
  rfid.PCD_Init();      // Init MFRC522 

  for (byte i = 0; i < 6; i++) 
    {  key.keyByte[i] = 0xFF;
    }

  Serial.println(F("This code scan the MIFARE Classsic NUID."));
  Serial.print(F("Using the following key:"));
  printHex(key.keyByte, MFRC522::MF_KEY_SIZE);
}
// ------------------------------------------------------------------
void printHex(byte *buffer, byte bufferSize) {
  for (byte i = 0; i < bufferSize; i++) {
    Serial.print(buffer[i] < 0x10 ? " 0" : " ");
    Serial.print(buffer[i], HEX);
  }
}
void printDec(byte *buffer, byte bufferSize) {
  for (byte i = 0; i < bufferSize; i++) {
    Serial.print(buffer[i] < 0x10 ? " 0" : " ");
    Serial.print(buffer[i], DEC);
  }
}
//------------------------------------------------------------------

void loop() {

  // Buscamos tarjetas
  if ( ! rfid.PICC_IsNewCardPresent())
    return;

  // SI la encuentra la leemos
  if ( ! rfid.PICC_ReadCardSerial())
    return;

  Serial.print(F("PICC type: "));
  MFRC522::PICC_Type piccType = rfid.PICC_GetType(rfid.uid.sak);
  Serial.println(rfid.PICC_GetTypeName(piccType));

  // Check is the PICC of Classic MIFARE type
  if (piccType != MFRC522::PICC_TYPE_MIFARE_MINI &&  
    piccType != MFRC522::PICC_TYPE_MIFARE_1K &&
    piccType != MFRC522::PICC_TYPE_MIFARE_4K) 
      {
        Serial.println(F("Your tag is not of type MIFARE Classic."));
        return;
      }

  if (rfid.uid.uidByte[0] != nuidPICC[0] || 
    rfid.uid.uidByte[1] != nuidPICC[1] || 
    rfid.uid.uidByte[2] != nuidPICC[2] || 
    rfid.uid.uidByte[3] != nuidPICC[3] ) 
    {
        Serial.println(F("A new card has been detected."));
    
        Serial.println(F("The NUID tag is:"));
        Serial.print(F("In hex: "));
        printHex(rfid.uid.uidByte, rfid.uid.size);
        Serial.println();
        Serial.print(F("In dec: "));
        printDec(rfid.uid.uidByte, rfid.uid.size);
        Serial.println();
     
       rfid.PICC_HaltA();
       rfid.PCD_StopCrypto1();
    }
    delay(600);
}
