# Fritzing sketch Practica#6Control-Remoto (saved by Fritzing 0.9.2b)

parts:
  S1 = H-Bridge with L298N
  J1 = Basic Servo
  M1 = DC Motor
  M2 = DC Motor
  Parte2 = HC-SR04
  Power_plug1 = Power plug
  Parte1 = Arduino Uno (Rev3)
  Parte3 = Bluetooth Mate Silver
  VCC1 = Battery block 9V
  VCC2 = Battery block 9V

nets:
  N1: S1.12V, VCC2.+
  GND: S1.GND, J1.gnd, Parte2.Gnd, Parte1.GND, Parte3.GND, VCC2.-
  N2: S1.ENA, Parte1.D2
  N3: S1.IN1, Parte1.D3_PWM
  N4: S1.IN2, Parte1.D4
  N5: S1.IN3, Parte1.D5_PWM
  N6: S1.IN4, Parte1.D6_PWM
  N7: S1.ENB, Parte1.D7
  N8: S1.M1-01, M2.pin_2
  VCC: S1.M1-02, S1.M2-01, S1.M2-02, S1.ENA-5V, J1.vcc, M1.pin_1, M1.pin_2, M2.pin_1, Parte2.Vcc, Parte1.5V, Parte3.VCC
  N9: J1.pulse, Parte1.D8
  N10: Parte2.Trig, Parte1.D10_PWM/SS
  N11: Parte2.Echo, Parte1.D9_PWM
  N12: Power_plug1.GND, VCC1.-
  N13: Power_plug1.VCC, VCC1.+
  N14: Parte1.D0/RX, Parte3.RX_5V
  N15: Parte1.D1/TX, Parte3.TX_5V

custom parts:
  H-Bridge with L298N: h-bridge
  HC-SR04: HC-SR04 ultrasonic distance sensor

// code stored in the sketch: vehiculo-blue.ino
#include <Ultrasonic.h>  //Librer?a del sensor ultras?nico
#include <Servo.h>  //Librer?a de servo motor
#include <PuenteH.h> //Librer?a de shield puente H

////* Declaraci?n de variables y pines*///
const int ENA = 2; const int IN1 = 3; const int IN2 = 4;// Motor A
const int ENB = 7; const int IN3 = 6; const int IN4 = 5;// Motor B
PuenteH puenteH(PuenteH::L298);/// Instancia a clase PuenteH
int distancia=0, distancia_izq=0, distancia_der=0;  // Variables para guardar las distancias
Ultrasonic ultrasonic(10,9); // ( PIN de disparo, PIN de eco)
Servo servo;  //Declaraci?n de objetivo tipo Servo
int estado = 'g';         // inicia detenido

void setup(){
  Serial.begin(9600);
  puenteH.setMotor1(ENA, IN1, IN2);
  puenteH.setMotor2(ENB, IN3, IN4);
  puenteH.initMotors();
  servo.attach(8);  
}

void loop (){
  if(Serial.available()>0){        // lee el bluetooth y almacena en estado
      estado = Serial.read();
  }
  if(estado=='a'){           // Boton desplazar al Frente
   	 puenteH.goForward(200);
  }
  if(estado=='b'){          // Boton IZQ 
     puenteH.turnLeft(200);     
  }
  if(estado=='c'){         // Boton Parar
     puenteH.stop();
  }
  if(estado=='d'){          // Boton DER
     puenteH.turnRight(200);
  } 
  
  if(estado=='e'){          // Boton Reversa
     puenteH.goBackward(200);
  }
  if (estado =='f'){          // Boton ON se mueve sensando distancia 
 
  }
  if  (estado=='g'){          // Boton OFF, detiene los motores no hace nada 
  }  
}
