# Fritzing sketch Practica#5Vehiculo (saved by Fritzing 0.9.2b)

parts:
  S1 = H-Bridge with L298N
  J1 = Basic Servo
  M1 = DC Motor
  M2 = DC Motor
  Parte2 = HC-SR04
  Parte1 = Arduino Uno (Rev3)
  VCC1 = Battery block 9V
  Power_plug1 = Power plug
  VCC2 = Battery block 9V

nets:
  N1: S1.12V, VCC2.+
  GND: S1.GND, J1.gnd, Parte2.Gnd, Parte1.GND, VCC2.-
  N2: S1.ENA, Parte1.D2
  N3: S1.IN1, Parte1.D3_PWM
  N4: S1.IN2, Parte1.D4
  N5: S1.IN3, Parte1.D5_PWM
  N6: S1.IN4, Parte1.D6_PWM
  N7: S1.ENB, Parte1.D7
  N8: S1.M1-01, M2.pin_2
  VCC: S1.M1-02, S1.M2-01, S1.M2-02, S1.ENA-5V, S1.ENB-5V, J1.vcc, M1.pin_1, M1.pin_2, M2.pin_1, Parte2.Vcc, Parte1.5V
  N9: J1.pulse, Parte1.D8
  N10: Parte2.Trig, Parte1.D10_PWM/SS
  N11: Parte2.Echo, Parte1.D9_PWM
  N12: VCC1.-, Power_plug1.GND
  N13: VCC1.+, Power_plug1.VCC

custom parts:
  H-Bridge with L298N: h-bridge
  HC-SR04: HC-SR04 ultrasonic distance sensor

// code stored in the sketch: Vehiculo.ino
#include <Ultrasonic.h>  //Librer?a del sensor ultras?nico
#include <Servo.h>  //Librer?a de servo motor
#include <PuenteH.h> //Librer?a de shield puente H

////* Declaraci?n de variables y pines*///
const int ENA = 2; const int IN1 = 3; const int IN2 = 4;// Motor A
const int ENB = 7; const int IN3 = 6; const int IN4 = 5;// Motor B
PuenteH puenteH(PuenteH::L298);/// Instancia a clase PuenteH
int distancia=0, distancia_izq=0, distancia_der=0;  // Variables para guardar las distancias
Ultrasonic ultrasonic(10,9); // ( PIN de disparo, PIN de eco)
Servo servo;  //Declaraci?n de objetivo tipo Servo

void setup(){
  Serial.begin(9600);
  puenteH.setMotor1(ENA, IN1, IN2);
  puenteH.setMotor2(ENB, IN3, IN4);
  puenteH.initMotors();
  servo.attach(8);  
}

void loop (){
  servo.write(95);  //Movemos el servomotor a una posici?n intermedia para que siempre inicie viendo al frente  
  /*El robot avanza hacia adelante*/
  puenteH.goForward(200);
  Serial.println(ultrasonic.Ranging(CM));
  delay(200);
  distancia=ultrasonic.Ranging(CM);  
  if (distancia <=10) //Comparaci?n de distancia, menor o igual a 10 cm{
    puenteH.stop();
    delay(500);
    Serial.print(ultrasonic.Ranging(CM));
    servo.write(8);  // Llevamos el servomotor a la derecha
    delay(500);
    distancia_der=ultrasonic.Ranging(CM);  // Se mide y guarda la distancia a la derecha
    delay(1000);
    Serial.print("distancia a la derecha: ");
    Serial.println(distancia_der);
    servo.write(180);  //Llevamos el servomotor a la izquierda
    delay(500);
    distancia_izq=ultrasonic.Ranging(CM);  // See mide y guarda la distancia a la izquierda
    delay(1000);
    Serial.print("distancia a la izquierda: ");
    Serial.println(distancia_izq);
    delay(1500);    
    // Comparaci?n entre la distancia de la izquierda y la derecha
    if(distancia_der > distancia_izq){
      puenteH.turnLeft(200);
    }
    else if (distancia_izq > distancia_der){
      puenteH.turnRight(200);
    }
    delay(1000);    
    //Reseteo de las variables que se comparan
    distancia_izq=0;
    distancia_der=0;
  }
  else{
    puenteH.goForward(200);
  }  
}
