# Fritzing sketch Practica5 (saved by Fritzing 0.9.0b)
breadboards: 1

parts:
  Parte1 = Arduino Uno (Rev3)
  LED1 = LED - 5mm [color="Red (633nm)" package="5 mm [THT]"]
  S1 = Pushbutton [package=THT]
  R1 = Resistor [tolerance=±5% resistance=1k package=THT]

nets:
  N1: Parte1.D13/SCK, LED1.anode
  N2: Parte1.GND, LED1.cathode, S1.leg0
  N3: Parte1.D2, S1.leg1, R1.Pin_0
  N4: Parte1.5V, R1.Pin_1
