# Fritzing sketch Practica6 (saved by Fritzing 0.9.0b)
breadboards: 1

parts:
  R1 = Resistor [tolerance=±5% resistance=220 package=THT]
  R3 = Resistor [tolerance=±5% resistance=220 package=THT]
  R2 = Resistor [tolerance=±5% resistance=220 package=THT]
  LED1 = RGB LED (com. cathode, rgb) [package="5 mm [THT]"]
  Parte1 = Arduino Uno (Rev3)

nets:
  N1: R1.Pin_0, LED1.red_anode
  N2: R1.Pin_1, Parte1.D9_PWM
  N3: R3.Pin_0, LED1.green_anode
  N4: R3.Pin_1, Parte1.D10_PWM/SS
  N5: R2.Pin_0, LED1.blue_anode
  N6: R2.Pin_1, Parte1.D11_PWM/MOSI
  N7: LED1.common_cathode, Parte1.5V
