# Fritzing sketch Practica7 (saved by Fritzing 0.9.0b)
breadboards: 1

parts:
  Parte1 = Arduino Uno (Rev3)
  LED2 = LED - 5mm [color="Red (633nm)" package="5 mm [THT]"]
  LED7 = LED - 5mm [color="Red (633nm)" package="5 mm [THT]"]
  LED6 = LED - 5mm [color="Red (633nm)" package="5 mm [THT]"]
  LED3 = LED - 5mm [color="Red (633nm)" package="5 mm [THT]"]
  LED5 = LED - 5mm [color="Red (633nm)" package="5 mm [THT]"]
  LED4 = LED - 5mm [color="Red (633nm)" package="5 mm [THT]"]
  LED8 = LED - 5mm [color="Red (633nm)" package="5 mm [THT]"]
  LED1 = LED - 5mm [color="Red (633nm)" package="5 mm [THT]"]
  R8 = Resistor [tolerance=±5% resistance=220 package=THT]
  R6 = Resistor [tolerance=±5% resistance=220 package=THT]
  R5 = Resistor [tolerance=±5% resistance=220 package=THT]
  R1 = Resistor [tolerance=±5% resistance=220 package=THT]
  R4 = Resistor [tolerance=±5% resistance=220 package=THT]
  R3 = Resistor [tolerance=±5% resistance=220 package=THT]
  R2 = Resistor [tolerance=±5% resistance=220 package=THT]
  R7 = Resistor [tolerance=±5% resistance=220 package=THT]

nets:
  N1: Parte1.D8, R7.Pin_1
  N2: Parte1.D9_PWM, R8.Pin_1
  N3: Parte1.GND, LED2.cathode, LED7.cathode, LED6.cathode, LED3.cathode, LED5.cathode, LED4.cathode, LED8.cathode, LED1.cathode
  N4: Parte1.D2, R1.Pin_1
  N5: Parte1.D3_PWM, R2.Pin_1
  N6: Parte1.D4, R3.Pin_1
  N7: Parte1.D5_PWM, R4.Pin_1
  N8: Parte1.D6_PWM, R5.Pin_1
  N9: Parte1.D7, R6.Pin_1
  N10: LED2.anode, R2.Pin_0
  N11: LED7.anode, R7.Pin_0
  N12: LED6.anode, R6.Pin_0
  N13: LED3.anode, R3.Pin_0
  N14: LED5.anode, R5.Pin_0
  N15: LED4.anode, R4.Pin_0
  N16: LED8.anode, R8.Pin_0
  N17: LED1.anode, R1.Pin_0
