# Fritzing sketch Practica8 (saved by Fritzing 0.9.0b)
breadboards: 1

parts:
  Parte1 = Arduino Uno (Rev3)
  R1 = Resistor [tolerance=±5% resistance=1k package=THT]
  M1 = DC Motor  # not connected
  R2 = Rotary Potentiometer (Small) [maximum_resistance=10kΩ package=THT]
  D1 = Rectifier Diode [part_number=1N4001 package="300 mil [THT]"]
  Q1 = NPN-Transistor [package="TO92 [THT]"]

nets (from the breadboard view):
  N1: Parte1.A0, R2.wiper
  N2: Parte1.D10_PWM/SS, R1.Pin_0
  N3: Parte1.GND, R2.leg1, Q1.C
  N4: Parte1.5V, R2.leg2, D1.cathode
  N5: R1.Pin_1, Q1.B
  N6: D1.anode, Q1.E
